# Fritzing sketch mkr-mlx90614-sensor-circuit-diagram (saved by Fritzing 0.9.4)
breadboards: 1

parts:
  Part1 = Arduino MKR WiFi 1010
  Mod1 = gy-906

nets:
  N1: Part1.D11_SDA, Mod1.SDA
  N2: Part1.D12_SCL, Mod1.SCL
  GND: Part1.GND, Mod1.GND
  VCC: Part1.VCC, Mod1.VIN

custom parts:
  Arduino MKR WiFi 1010: This is the newest version of the MKR 1000 WIFI, but with an ESP32 module on board made by U-BLOX.
  gy-906: gy-906 Non-contact PIR I2C interface temperature sensor breakout board.
