# Fritzing sketch uno-mlx90614-sensor-circuit-diagram (saved by Fritzing 0.9.4)
breadboards: 1

parts:
  Part2 = Arduino Uno (Rev3)
  Mod1 = gy-906

nets:
  GND: Part2.GND, Mod1.GND
  N1: Part2.A4/SDA, Mod1.SDA
  N2: Part2.A5/SCL, Mod1.SCL
  3V3: Part2.3V3, Mod1.VIN

custom parts:
  gy-906: gy-906 Non-contact PIR I2C interface temperature sensor breakout board.
