# Fritzing sketch esp32-mlx90614-sensor-circuit-diagram (saved by Fritzing 0.9.4)
breadboards: 1

parts:
  MCU1 = Wemos Lolin32lite
  Mod1 = gy-906

nets:
  N1: MCU1.pin_13, Mod1.GND
  N2: MCU1.pin_20, Mod1.SDA
  N3: MCU1.pin_23, Mod1.SCL
  N4: MCU1.pin_28, Mod1.VIN

custom parts:
  Wemos Lolin32lite: Wemos Lolinlite32 wifi and bluetooth board based on the ESP-32 cpu, digital I/Os 19, analog inputs 6, clock 240mhz, Flash 4Mbytes, lipo battery charger (500ma connection broken out on breadboard but not pcb), usb.
  gy-906: gy-906 Non-contact PIR I2C interface temperature sensor breakout board.
