# Fritzing sketch esp8266-mlx90614-sensor-circuit-diagram (saved by Fritzing 0.9.4)
breadboards: 1

parts:
  WeMos_D1_Mini1 = WeMos D1 Mini
  Mod2 = gy-906

nets:
  3V3: WeMos_D1_Mini1.3V3, Mod2.VIN
  N1: WeMos_D1_Mini1.D1, Mod2.SCL
  N2: WeMos_D1_Mini1.D2, Mod2.SDA
  N3: WeMos_D1_Mini1.G, Mod2.GND

custom parts:
  gy-906: gy-906 Non-contact PIR I2C interface temperature sensor breakout board.
