# Fritzing sketch rpi-mlx90614-sensor-circuit-diagram (saved by Fritzing 0.9.4)
breadboards: 1

parts:
  Raspberry_Pi_1 = Raspberry Pi 3 [part_number=RPI-3-V1.2]
  Mod1 = gy-906

nets:
  3V3: Raspberry_Pi_1.3v3, Mod1.VIN
  N1: Raspberry_Pi_1.GPIO2, Mod1.SDA
  N2: Raspberry_Pi_1.GPIO3, Mod1.SCL
  GND: Raspberry_Pi_1.GND, Mod1.GND

custom parts:
  gy-906: gy-906 Non-contact PIR I2C interface temperature sensor breakout board.
